# Fritzing sketch sur24 (saved by Fritzing 0.9.3b)
perfboards: 1

parts:
  A1 = A9G GSM/GPRS+GPS Module
  M1 = DOIT Esp32 DevKit v1 (30 pins long, 11 pins width) [part_number=ESP32S-PIN30]
  J1 = Camdenboss CTB0158-2 [part_number=CTB0158-2 package=THT]
  OLED_I2C1 = OLED 128x64 I2C Monochrome Display  # not connected
  J2 = Camdenboss CTB0158-4 [part_number=CTB0158-4 package=THT]
  J3 = Camdenboss CTB0158-5 [part_number=CTB0158-5 package=THT]

nets:
  N1: A1.Pin_3, A1.Pin_28
  N2: A1.Pin_4, A1.Pin_5, A1.Pin_27, M1.GND, J1.pin1, J2.pin2, J3.pin1
  N3: A1.Pin_6, M1.VIN, J1.pin2, J2.pin1
  N4: A1.Pin_17, M1.TX2
  N5: A1.Pin_18, M1.RX2
  N6: M1.D32, J3.pin5
  N7: M1.D33, J3.pin4
  N8: M1.D25, J3.pin3
  N9: M1.D26, J3.pin2
  N10: M1.D14, J2.pin4
  N11: M1.D13, J2.pin3

notes:
  sw SMS
  sw Alarma
  sw Izq
  sw Dcha
  GND switches
  Rele izq
  Rele Dcha
  GND Rele
  +5v Rele
  GND
  5v Vin

custom parts:
  A9G GSM/GPRS+GPS Module: A9G is a complete quad-band GSM/GPRS+GPS module based on the RDA8955 chip.
  DOIT Esp32 DevKit v1 (30 pins long, 11 pins width): The DOIT Esp32 DevKit v1 is one of the development board created by DOIT to evaluate the ESP-WROOM-32 module. It is based on the ESP32 microcontroller that boasts Wifi, Bluetooth, Ethernet and Low Power support all in a single chip. (vanepp) made breadboard work, adjusted pin numbering and labels and reduced size of schematic and cleaned up pcb. This chip is 30pins long (2 x15) and 11 pins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
